// Logisim project ipc.circ as structural Verilog: 2 circuits, main circuit main
module main (
);

  wire acz, adc, add, add_out, adder_1_cout, amov, and_2_out, and_3_out, and_4_out, and_5_out, and_6_out,
       and_7_out, and_8_out, and_9_out, and_10_out, and_11_out, and_12_out, and_14_out, and_15_out,
       and_16_out, and_17_out, and_18_out, and_19_out, and_20_out, and_21_out, and_22_out, and_23_out,
       and_24_out, and_25_out, and_26_out, and_27_out, and_28_out, and_29_out, and_30_out, and_31_out,
       and_32_out, and_33_out, and_34_out, and_35_out, and_36_out, and_37_out, bca, bnc, bnz, bpa, branch,
       bsi, button_1_out, button_2_out, button_3_out, button_4_out, button_5_out, button_6_out, bze, carryt,
       clc, clock_1_out, clockt, ctrl_alu, ctrl_reg_in, ctrl_reg_out, ctrl_setting_carry, ctrl_sub,
       ctrl_using_adder, cur_byte_im, decoder_2_out0, decoder_2_out1, decoder_2_out2, decoder_2_out3,
       decoder_2_out4, decoder_2_out5, decoder_2_out6, decoder_2_out7, hlt, i_and, i_in, i_nor, i_out, i_ror,
       i_xor, im_to_reg, ima, imr, jmp, ld, nop, nor_2_out, nor_3_out, nor_4_out, nor_5_out, not_1_out,
       not_2_out, not_3_out, or_1_out, or_3_out, or_4_out, or_5_out, or_6_out, or_7_out, or_8_out, parityt,
       pop, push, rmov, sbc, signt, spc, stc, str, sub, undriven, xor_1_out, xor_10_out, zerot;
  wire [0:0] ram_1_data_2;
  wire [2:0] multiplexer_2_out, register_1_q;
  wire [6:0] ram_1_data;
  wire [7:0] ac, adder_1_out, and_13_out, bph, bpl, controlled_buffer_1_out, inputd, marh, marl,
       multiplexer_3_out, multiplexer_4_out, multiplexer_5_out, nor_1_out, out_d, prog_out, r0, r1, sph, spl,
       xor_2_out;
  wire [15:0] multiplexer_1_out, pc;

  or or_1 (or_1_out, push, pop);
  Multiplexer #(.width(16)) multiplexer_1 (
    .in0({marh, marl}), .in1({sph, spl}), .out(multiplexer_1_out), .sel(or_1_out));
  Clock clock_1 (.out(clock_1_out));
  and and_1 (clockt, ~hlt, clock_1_out);  // AND_Gate
  Counter #(.max('hffff), .trigger("falling"), .width(16)) counter_1 (
    .load(branch), .D(multiplexer_1_out), .count(1'b1), .Q(pc), .up(1'b1), .clk(clockt));  // open: carry, clr
  ROM #(.addrWidth(16)) rom_1 (.addr(pc), .data(prog_out));
  and and_2 (and_2_out, bca, carryt);
  and and_3 (and_3_out, bnc, ~carryt);  // AND_Gate
  and and_4 (and_4_out, bze, zerot);
  and and_5 (and_5_out, bnz, ~zerot);  // AND_Gate
  and and_6 (and_6_out, bsi, signt);
  and and_7 (and_7_out, bpa, parityt);
  RAM #(.addrWidth(16), .databus("bidir"), .enables("line")) ram_1 (
    .addr(multiplexer_1_out), .data({ram_1_data, ram_1_data_2[0]}));  // open: we, oe, clk
  or or_2 (branch, jmp, and_2_out, and_3_out, and_4_out, and_5_out, and_6_out, and_7_out);
  not not_1 (not_1_out, cur_byte_im);
  Decoder #(.select(5)) decoder_1 (
    .out0(add), .out1(sub), .out2(adc), .out3(sbc), .out4(i_ror), .out5(i_nor), .out6(i_and), .out7(i_xor),
    .out9(stc), .out10(clc), .out11(rmov), .out12(amov), .out13(jmp), .out14(bca), .out15(bnc), .out16(bze),
    .out17(bnz), .out18(bsi), .out19(bpa), .out20(acz), .out21(ima), .out22(imr), .out23(spc), .out24(str),
    .out25(ld), .out26(i_in), .out27(i_out), .out28(nop), .out29(hlt), .out30(push), .out31(pop),
    .sel(prog_out[4:0]), .en(not_1_out));  // open: out8
  Pull_Resistor pull_resistor_1 (.node({ram_1_data, ram_1_data_2[0]}));
  or setting_carry (ctrl_setting_carry, ctrl_using_adder, i_ror);
  or using_adder (ctrl_using_adder, add_out, ctrl_sub);
  or u_add (add_out, add, adc);
  or or_3 (or_3_out, ima, imr);
  and and_8 (and_8_out, or_3_out, ~cur_byte_im);  // AND_Gate
  and and_9 (and_9_out, carryt, sbc);
  or register_out (ctrl_reg_out, ctrl_alu, rmov, str, push, i_out);
  or alu (ctrl_alu, ctrl_setting_carry, i_ror, i_nor, i_and);
  or u_sub (ctrl_sub, sub, sbc);
  D_Flip_Flop #(.trigger("falling")) d_ff_1 (.D(and_8_out), .clk(clockt), .Q(cur_byte_im));  // open: Qn, preset, reset
  Register #(.width(4)) register_1 (
    .D({imr, prog_out[7:5]}), .en(1'b1), .clk(clockt), .Q({im_to_reg, register_1_q}));  // open: clr
  xor xor_1 (xor_1_out, and_9_out, ctrl_sub);
  xor xor_2 (xor_2_out[0], ram_1_data_2[0], ctrl_sub);
  xor xor_3 (xor_2_out[1], ram_1_data[0], ctrl_sub);
  or register_in (ctrl_reg_in, and_10_out, amov, i_in, ld, pop);
  and and_10 (and_10_out, im_to_reg, cur_byte_im);
  Multiplexer #(.width(3)) multiplexer_2 (
    .in0(prog_out[7:5]), .in1(register_1_q), .out(multiplexer_2_out), .sel(cur_byte_im));
  and and_11 (and_11_out, adc, carryt);
  or or_4 (or_4_out, and_11_out, and_12_out);
  and and_12 (and_12_out, xor_1_out, ctrl_sub);
  Adder adder_1 (.a(ac), .b(xor_2_out), .out(adder_1_out), .cin(or_4_out), .cout(adder_1_cout));
  xor xor_4 (xor_2_out[2], ram_1_data[1], ctrl_sub);
  xor xor_5 (xor_2_out[3], ram_1_data[2], ctrl_sub);
  assign nor_1_out = ~({ram_1_data, ram_1_data_2[0]} | ac);  // NOR_Gate nor_1, 8 bits wide
  assign and_13_out = {ram_1_data, ram_1_data_2[0]} & ac;  // AND_Gate and_13, 8 bits wide
  Decoder #(.enable("false"), .select(3)) decoder_2 (
    .out0(decoder_2_out0), .out1(decoder_2_out1), .out2(decoder_2_out2), .out3(decoder_2_out3),
    .out4(decoder_2_out4), .out5(decoder_2_out5), .out6(decoder_2_out6), .out7(decoder_2_out7),
    .sel(multiplexer_2_out));
  assign controlled_buffer_1_out = ctrl_using_adder ? adder_1_out : 8'bz;  // Controlled_Buffer controlled_buffer_1
  xor xor_6 (xor_2_out[4], ram_1_data[3], ctrl_sub);
  xor xor_7 (xor_2_out[5], ram_1_data[4], ctrl_sub);
  assign controlled_buffer_1_out = i_ror ? {carryt, ram_1_data} : 8'bz;  // Controlled_Buffer controlled_buffer_2
  assign controlled_buffer_1_out = i_nor ? nor_1_out : 8'bz;  // Controlled_Buffer controlled_buffer_3
  assign controlled_buffer_1_out = i_and ? and_13_out : 8'bz;  // Controlled_Buffer controlled_buffer_4
  xor xor_8 (xor_2_out[6], ram_1_data[5], ctrl_sub);
  xor xor_9 (xor_2_out[7], ram_1_data[6], ctrl_sub);
  xor xor_10 (xor_10_out, adder_1_cout, ctrl_sub);
  not not_2 (not_2_out, ctrl_using_adder);
  nor nor_2 (nor_2_out, controlled_buffer_1_out[7], controlled_buffer_1_out[6]);
  nor nor_3 (nor_3_out, controlled_buffer_1_out[5], controlled_buffer_1_out[4]);
  and and_14 (and_14_out, nor_2_out, nor_3_out);
  assign {ram_1_data, ram_1_data_2[0]} = cur_byte_im ? prog_out : 8'bz;  // Controlled_Buffer controlled_buffer_5
  and and_15 (and_15_out, xor_10_out, ctrl_using_adder);
  or or_5 (or_5_out, and_15_out, and_16_out);
  and and_16 (and_16_out, ram_1_data_2[0], not_2_out);
  nor nor_4 (nor_4_out, controlled_buffer_1_out[3], controlled_buffer_1_out[2]);
  nor nor_5 (nor_5_out, controlled_buffer_1_out[1], controlled_buffer_1_out[0]);
  and and_17 (and_17_out, nor_4_out, nor_5_out);
  and and_18 (and_18_out, and_14_out, and_17_out);
  and and_19 (and_19_out, ctrl_alu, clockt);
  assign out_d = i_out ? {ram_1_data, ram_1_data_2[0]} : 8'bz;  // Controlled_Buffer controlled_buffer_6
  and and_20 (and_20_out, decoder_2_out7, ctrl_reg_out);
  Multiplexer #(.width(8)) multiplexer_3 (
    .in0({ram_1_data, ram_1_data_2[0]}), .in1(pc[15:8]), .out(multiplexer_3_out), .sel(spc));
  and and_21 (and_21_out, ctrl_reg_in, decoder_2_out7);
  and and_22 (and_22_out, decoder_2_out6, ctrl_reg_out);
  Multiplexer #(.width(8)) multiplexer_4 (
    .in0({ram_1_data, ram_1_data_2[0]}), .in1(pc[7:0]), .out(multiplexer_4_out), .sel(spc));
  or or_6 (or_6_out, spc, and_23_out);
  and and_23 (and_23_out, ctrl_reg_in, decoder_2_out6);
  and and_24 (and_24_out, decoder_2_out5, ctrl_reg_out);
  and and_25 (and_25_out, ctrl_reg_in, decoder_2_out5);
  and and_26 (and_26_out, decoder_2_out4, ctrl_reg_out);
  and and_27 (and_27_out, ctrl_reg_in, decoder_2_out4);
  and and_28 (and_28_out, decoder_2_out3, ctrl_reg_out);
  and and_29 (and_29_out, ctrl_reg_in, decoder_2_out3);
  and and_30 (and_30_out, decoder_2_out2, ctrl_reg_out);
  and and_31 (and_31_out, ctrl_reg_in, decoder_2_out2);
  and and_32 (and_32_out, decoder_2_out1, ctrl_reg_out);
  and and_33 (and_33_out, ctrl_reg_in, decoder_2_out1);
  and and_34 (and_34_out, decoder_2_out0, ctrl_reg_out);
  and and_35 (and_35_out, decoder_2_out0, ctrl_reg_in);
  Multiplexer #(.width(8)) multiplexer_5 (
    .in0({ram_1_data, ram_1_data_2[0]}), .in1(controlled_buffer_1_out), .out(multiplexer_5_out),
    .sel(ctrl_alu));
  or or_7 (or_7_out, ctrl_alu, and_36_out, rmov);
  and and_36 (and_36_out, not_3_out, cur_byte_im);
  not not_3 (not_3_out, im_to_reg);
  Pull_Resistor pull_resistor_2 (.node(controlled_buffer_1_out));
  Register u_marh (.D(multiplexer_3_out), .en(or_8_out), .clk(clockt), .Q(marh));  // open: clr
  or or_8 (or_8_out, spc, and_21_out);
  Register u_marl (.D(multiplexer_4_out), .en(or_6_out), .clk(clockt), .Q(marl));  // open: clr
  Register u_sph (.D({ram_1_data, ram_1_data_2[0]}), .en(and_25_out), .clk(clockt), .Q(sph));  // open: clr
  Register u_spl (.D({ram_1_data, ram_1_data_2[0]}), .en(and_27_out), .clk(clockt), .Q(spl));  // open: clr
  Register u_bph (.D({ram_1_data, ram_1_data_2[0]}), .en(and_29_out), .clk(clockt), .Q(bph));  // open: clr
  Register u_bpl (.D({ram_1_data, ram_1_data_2[0]}), .en(and_31_out), .clk(clockt), .Q(bpl));  // open: clr
  Register u_r1 (.D({ram_1_data, ram_1_data_2[0]}), .en(and_33_out), .clk(clockt), .Q(r1));  // open: clr
  Register u_r0 (.D({ram_1_data, ram_1_data_2[0]}), .en(and_35_out), .clk(clockt), .Q(r0));  // open: clr
  Register u_ac (.D(multiplexer_5_out), .en(or_7_out), .clk(clockt), .Q(ac));  // open: clr
  D_Flip_Flop carryf (.D(or_5_out), .clk(and_37_out), .Q(carryt), .preset(clc), .reset(stc));  // open: Qn
  and and_37 (and_37_out, ctrl_setting_carry, clockt);
  D_Flip_Flop zerof (.D(and_18_out), .clk(and_19_out), .Q(zerot));  // open: Qn, preset, reset
  D_Flip_Flop signf (.D(controlled_buffer_1_out[7]), .clk(and_19_out), .Q(signt));  // open: Qn, preset, reset
  D_Flip_Flop parityf (.D(controlled_buffer_1_out[0]), .clk(and_19_out), .Q(parityt));  // open: Qn, preset, reset
  assign {ram_1_data, ram_1_data_2[0]} = i_in ? inputd : 8'bz;  // Controlled_Buffer controlled_buffer_7
  assign {ram_1_data, ram_1_data_2[0]} = and_20_out ? marh : 8'bz;  // Controlled_Buffer controlled_buffer_8
  assign {ram_1_data, ram_1_data_2[0]} = and_22_out ? marl : 8'bz;  // Controlled_Buffer controlled_buffer_9
  assign {ram_1_data, ram_1_data_2[0]} = and_24_out ? sph : 8'bz;  // Controlled_Buffer controlled_buffer_10
  assign {ram_1_data, ram_1_data_2[0]} = and_26_out ? spl : 8'bz;  // Controlled_Buffer controlled_buffer_11
  assign {ram_1_data, ram_1_data_2[0]} = and_28_out ? bph : 8'bz;  // Controlled_Buffer controlled_buffer_12
  assign {ram_1_data, ram_1_data_2[0]} = and_30_out ? bpl : 8'bz;  // Controlled_Buffer controlled_buffer_13
  assign {ram_1_data, ram_1_data_2[0]} = and_32_out ? r1 : 8'bz;  // Controlled_Buffer controlled_buffer_14
  assign {ram_1_data, ram_1_data_2[0]} = and_34_out ? r0 : 8'bz;  // Controlled_Buffer controlled_buffer_15
  assign {ram_1_data, ram_1_data_2[0]} = amov ? ac : 8'bz;  // Controlled_Buffer controlled_buffer_16
  // Probe on r0
  // Probe on spl
  // Probe on prog_out
  input_cont input_cont_1 (
    .in_0(button_1_out), .in_1(button_3_out), .in_2(button_2_out), .in_3(button_4_out), .in_4(button_5_out),
    .in_sig(i_in), .in_5(button_6_out), .clock_input(clockt), .input_data(inputd));
  Button button_1 (.out(button_1_out));
  Button button_2 (.out(button_2_out));
  Button button_3 (.out(button_3_out));
  Button button_4 (.out(button_4_out));
  // Probe on r1
  // Probe on sph
  // Probe on ac
  Button button_5 (.out(button_5_out));
  // Probe on bpl
  // Probe on marl
  LED led_1 (.in(undriven));
  Button button_6 (.out(button_6_out));
  // Probe on bph
  // Probe on marh

  // Notes on the sheet:
  //   contents of rom_1 (hex, n*v repeats v):
  //   1a 1e f6 0 d6 0 10 b6 4 ab 6 f6 0 d6 30 11 b6 8 ab 6 f6 0 d6 3a 11 b6 1 ab 6 f6 0 d6 44 11 b6 2 ab 6
  //   f6 0 d6 4c 11 f6 0 d6 0 d b6 1 ab 20 2c f6 0 d6 0 d b6 1 2b a1 2c f6 0 d6 0 d 2b 20 2c f6 0 d6 0 d a
  //   24 2c f6 0 d6 0 d
  //   A
  //   B
  //   ROR
  //   Carry is set by Adder or ROR
endmodule

module input_cont (
  input  in_sig,
  input  clock_input,
  input  in_0,
  input  in_1,
  input  in_2,
  input  in_3,
  input  in_4,
  input  in_5,
  output [7:0] input_data
);

  wire and_1_out, or_1_out;
  wire [7:0] multiplexer_1_out, or_2_out, pull_resistor_1_node, pull_resistor_3_node, register_1_q;
  wire [7:6] pull_resistor_2_node;

  or or_1 (or_1_out, in_0, in_1, in_2, in_3, in_4, in_5);
  Pull_Resistor pull_resistor_1 (.node(pull_resistor_1_node));
  assign or_2_out = {pull_resistor_2_node, in_5, in_4, in_3, in_2, in_1, in_0} | register_1_q;  // OR_Gate or_2, 8 bits wide
  Pull_Resistor pull_resistor_2 (.node({pull_resistor_2_node, in_5, in_4, in_3, in_2, in_1, in_0}));
  and and_1 (and_1_out, ~or_1_out, in_sig);  // AND_Gate
  Register #(.trigger("falling")) register_1 (
    .D(multiplexer_1_out), .en(1'b1), .clk(clock_input), .Q(register_1_q));  // open: clr
  Multiplexer #(.width(8)) multiplexer_1 (
    .in0(or_2_out), .in1(pull_resistor_1_node), .out(multiplexer_1_out));  // open: sel
  Pull_Resistor pull_resistor_3 (.node(pull_resistor_3_node));
  // Probe on register_1_q
  Multiplexer #(.width(8)) multiplexer_2 (
    .in0(pull_resistor_3_node), .in1(register_1_q), .out(input_data));  // open: sel
endmodule
